# Fritzing sketch sg.png (saved by Fritzing 0.9.3b)
breadboards: 1

parts:
  Mod1 = zmpt101b
  U3 = ESP8266 NodeMCU LoLin module
  U9 = LCD-16X2 [package=lcd-16x2_nosilk]
  Mod2 = KY-012 Active Buzzer Module [package="Breakout board"]

nets:
  VCC: Mod1.VCC, U3.3V3, U9.VDD
  N1: Mod1.OUT, Mod1.GND#2, U3.A0
  GND: Mod1.GND#3, U3.GND, U9.VSS, U9.R_W, Mod2.-
  N2: U3.D0, U9.RS
  N3: U3.D1, U9.E
  N4: U3.D2, U9.DB4
  N5: U3.D3, U9.DB5
  N6: U3.D4, U9.DB6
  N7: U3.D5, U9.DB7
  N8: U3.D8, Mod2.S

custom parts:
  zmpt101b: Single phase ac active output voltate transformer module.
  ESP8266 NodeMCU LoLin module: ESP8266 based NodeMCU
  KY-012 Active Buzzer Module: Active Piezoelectric Buzzer Module KY-012, it produces single-tone sound when signal is high. (Special thanks to vanepp for fixing the PCB holes and other errors)
